# Fritzing sketch fritzing (saved by Fritzing 0.9.3b)
breadboards: 1

parts:
  Componente1 = Arduino Uno (Rev3)
  R1 = Resistor [tolerance=±5% resistance=220 package=THT]
  S1 = Pushbutton [package="[THT]"]
  LED1 = LED - 5mm [color="Blue (430nm)" package="5 mm [THT]"]
  R2 = Resistor [tolerance=±5% resistance=220 package=THT]
  J1 = Piezo Speaker

nets:
  N1: Componente1.D8, J1.pin2
  N2: Componente1.D13/SCK, LED1.anode
  N3: Componente1.D2, R1.Pin_1, S1.Pin_3, S1.Pin_4
  N4: Componente1.5V, S1.Pin_1, S1.Pin_2
  N5: Componente1.GND, R1.Pin_0, R2.Pin_1, J1.pin1
  N6: LED1.cathode, R2.Pin_0
